// Logisim project Mic-1.circ as structural Verilog: 17 circuits, main circuit main
module main (
);

  wire _4_to_16_Decoder_out_2, _4_to_16_Decoder_out_3, _4_to_16_Decoder_out_4, _4_to_16_Decoder_out_5,
       _4_to_16_Decoder_out_6, _4_to_16_Decoder_out_7, _4_to_16_Decoder_out_8, _4_to_16_Decoder_out_9,
       _4_to_16_Decoder_out_10, Shifter_p1, undriven_2;
  wire [2:0] Control_Store_jam, Control_Store_memory;
  wire [3:0] Control_Store_b_bus;
  wire [7:0] Control_Store_alu;
  wire [8:0] Control_Store_addr, Control_Store_c_bus;
  wire [31:0] H_probe, undriven;

  TOS TOS (.C_Bus_Enable(Control_Store_c_bus[6]), .B_Enable(_4_to_16_Decoder_out_9));  // open: Clock, Input, Output
  LV LV (.C_Bus_Enable(Control_Store_c_bus[4]), .B_Enable(_4_to_16_Decoder_out_7));  // open: Clock, Input, Output
  CPP CPP (.C_Bus_Enable(Control_Store_c_bus[5]), .B_Enable(_4_to_16_Decoder_out_8));  // open: Clock, Input, Output
  MAR MAR (.Enable(Control_Store_c_bus[0]));  // open: in_1, out_3, out_4
  MDR MDR (
    .in_4(Control_Store_c_bus[1]), .in_5(_4_to_16_Decoder_out_2));  // open: in_2, in_3, out_6, in_1, out_7, out_8
  PC PC (.in_2(Control_Store_c_bus[2]), .in_3(_4_to_16_Decoder_out_3));  // open: out_4, in_1, out_5, out_6
  MBR MBR (
    .B_Enable_Unsigned(_4_to_16_Decoder_out_5), .B_Enable_Signed(_4_to_16_Decoder_out_4));  // open: Input, Output_Unsigned, Output_Signed, Output, Probe
  SP SP (.C_Bus_Enable(Control_Store_c_bus[3]), .B_Enable(_4_to_16_Decoder_out_6));  // open: Clock, Input, Output
  OPC OPC (.C_Bus_Enable(Control_Store_c_bus[7]), .B_Enable(_4_to_16_Decoder_out_10));  // open: Clock, Input, Output
  H H (.Enable(Control_Store_c_bus[8]), .Probe(H_probe));  // open: in_1, Input, Output
  _32_bit_ALU ALU (.A(H_probe), .B(undriven), .in_2(undriven_2));  // open: out_6, out_5, Control
  _4_to_16_Decoder _4_to_16_Decoder (
    .in_1(Control_Store_b_bus), .out_2(_4_to_16_Decoder_out_2), .out_3(_4_to_16_Decoder_out_3),
    .out_4(_4_to_16_Decoder_out_4), .out_5(_4_to_16_Decoder_out_5), .out_6(_4_to_16_Decoder_out_6),
    .out_8(_4_to_16_Decoder_out_8), .out_9(_4_to_16_Decoder_out_9), .out_10(_4_to_16_Decoder_out_10),
    .out_7(_4_to_16_Decoder_out_7));
  // Shifter Shifter: pin names not known; wires that end beside it: Shifter_p1, Shifter_p1
  Control_Store Control_Store (
    .Addr(Control_Store_addr), .JAM(Control_Store_jam), .ALU(Control_Store_alu), .C_Bus(Control_Store_c_bus),
    .Memory(Control_Store_memory), .B_Bus(Control_Store_b_bus));  // open: in_1
endmodule

module SP (
  input  Clock,
  input  [31:0] Input,
  input  B_Enable,
  input  C_Bus_Enable,
  output [23:0] Output
);

  wire [31:0] SP_q;

  Register #(.width(32)) SP (.D(Input), .en(C_Bus_Enable), .Q(SP_q), .clk(Clock));  // open: clr
  assign Output = B_Enable ? SP_q[23:0] : 24'bz;  // Controlled_Buffer controlled_buffer_1
endmodule

module _4_to_16_Decoder (
  input  [3:0] in_1,
  output out_2,
  output out_3,
  output out_4,
  output out_5,
  output out_6,
  output out_7,
  output out_8,
  output out_9,
  output out_10
);

  wire undriven;

  Decoder #(.select(4)) decoder_1 (
    .out0(out_2), .out1(out_3), .out2(out_4), .out3(out_5), .out4(out_6), .out5(out_7), .out6(out_8),
    .out7(out_9), .out8(out_10), .sel(in_1), .en(undriven));  // open: out9, out10, out11, out12, out13, out14, out15
endmodule

module H (
  input  in_1,
  input  [31:0] Input,
  input  Enable,
  output [31:0] Output,
  output [31:0] Probe
);

  Register #(.width(32)) H (.D(Input), .en(Enable), .Q(Output), .clk(in_1));  // open: clr

  assign Probe = Output;

  // Notes on the sheet:
  //   Clock
endmodule

module ALU (
  input  Carry_In,
  input  A,
  input  B,
  input  [4:0] in_4,
  output out_5,
  output Carry_Out
);

  wire and_1_out, and_2_out, and_3_out, and_4_out, and_5_out, and_6_out, and_7_out, and_8_out, and_9_out,
       and_10_out, and_11_out, and_12_out, and_13_out, not_1_out, not_2_out, not_3_out, or_1_out, xor_2_out,
       xor_3_out;

  and and_1 (and_1_out, A, in_4[0]);
  and and_2 (and_2_out, B, in_4[2]);
  // XOR_Gate xor_1 has open pins: in0=and_1_out, in1=in_4[1], out=open
  not not_1 (not_1_out, in_4[3]);
  and and_3 (and_3_out, and_1_out, and_2_out);
  or or_1 (or_1_out, and_1_out, and_2_out);
  not not_2 (not_2_out, and_2_out);
  not not_3 (not_3_out, in_4[4]);
  and and_4 (and_4_out, not_1_out, not_3_out);
  and and_5 (and_5_out, not_1_out, in_4[4]);
  and and_6 (and_6_out, in_4[3], not_3_out);
  and and_7 (and_7_out, in_4[3], in_4[4]);
  and and_8 (and_8_out, and_3_out, and_4_out);
  and and_9 (and_9_out, or_1_out, and_5_out);
  and and_10 (and_10_out, not_2_out, and_6_out);
  and and_11 (and_11_out, and_2_out, and_7_out, and_1_out);
  xor xor_2 (xor_2_out, and_2_out, and_1_out);
  or or_2 (Carry_Out, and_11_out, and_12_out);
  and and_12 (and_12_out, xor_2_out, and_7_out, Carry_In);
  xor xor_3 (xor_3_out, Carry_In, xor_2_out);
  and and_13 (and_13_out, xor_3_out, and_7_out);
  or Result (out_5, and_8_out, and_9_out, and_10_out, and_13_out);

  // Notes on the sheet:
  //   EnA
  //   InverseA
  //   EnB
  //   Decoder
  //   F0
  //   F1
  //   Logic Unit
  //   Adder
endmodule

module _32_bit_ALU (
  input  [31:0] A,
  input  in_2,
  input  [31:0] B,
  input  [4:0] Control,
  output [31:0] out_5,
  output out_6
);

  wire n8_bit_alu_1_out_6, n8_bit_alu_2_out_6, n8_bit_alu_3_out_6;

  _8_Bit_ALU u_8_bit_alu_1 (
    .A(A[7:0]), .B(B[7:0]), .out_5(out_5[7:0]), .in_4(Control), .in_2(in_2), .out_6(n8_bit_alu_1_out_6));
  _8_Bit_ALU u_8_bit_alu_2 (
    .A(A[15:8]), .B(B[15:8]), .out_5(out_5[15:8]), .in_4(Control), .in_2(n8_bit_alu_1_out_6),
    .out_6(n8_bit_alu_2_out_6));
  _8_Bit_ALU u_8_bit_alu_3 (
    .A(A[23:16]), .B(B[23:16]), .out_5(out_5[23:16]), .in_4(Control), .in_2(n8_bit_alu_2_out_6),
    .out_6(n8_bit_alu_3_out_6));
  _8_Bit_ALU u_8_bit_alu_4 (
    .A(A[31:24]), .B(B[31:24]), .out_5(out_5[31:24]), .in_4(Control), .in_2(n8_bit_alu_3_out_6), .out_6(out_6));
endmodule

module _8_Bit_ALU (
  input  [7:0] A,
  input  in_2,
  input  [7:0] B,
  input  [4:0] in_4,
  output [7:0] out_5,
  output out_6
);

  wire alu_1_carry_out, alu_2_carry_out, alu_3_carry_out, alu_4_carry_out, alu_5_carry_out, alu_6_carry_out,
       alu_7_carry_out;

  ALU alu_1 (.A(A[0]), .B(B[0]), .out_5(out_5[7]), .Carry_In(in_2), .Carry_Out(alu_1_carry_out), .in_4(in_4));
  ALU alu_2 (
    .A(A[1]), .B(B[1]), .out_5(out_5[6]), .Carry_In(alu_1_carry_out), .Carry_Out(alu_2_carry_out), .in_4(in_4));
  ALU alu_3 (
    .A(A[2]), .B(B[2]), .out_5(out_5[5]), .Carry_In(alu_2_carry_out), .Carry_Out(alu_3_carry_out), .in_4(in_4));
  ALU alu_4 (
    .A(A[3]), .B(B[3]), .out_5(out_5[4]), .Carry_In(alu_3_carry_out), .Carry_Out(alu_4_carry_out), .in_4(in_4));
  ALU alu_5 (
    .A(A[4]), .B(B[4]), .out_5(out_5[3]), .Carry_In(alu_4_carry_out), .Carry_Out(alu_5_carry_out), .in_4(in_4));
  ALU alu_6 (
    .A(A[5]), .B(B[5]), .out_5(out_5[2]), .Carry_In(alu_5_carry_out), .Carry_Out(alu_6_carry_out), .in_4(in_4));
  ALU alu_7 (
    .A(A[6]), .B(B[6]), .out_5(out_5[1]), .Carry_In(alu_6_carry_out), .Carry_Out(alu_7_carry_out), .in_4(in_4));
  ALU alu_8 (.A(A[7]), .B(B[7]), .out_5(out_5[0]), .Carry_In(alu_7_carry_out), .Carry_Out(out_6), .in_4(in_4));
endmodule

module LV (
  input  Clock,
  input  [31:0] Input,
  input  B_Enable,
  input  C_Bus_Enable,
  output [23:0] Output
);

  wire [31:0] SP_q;

  Register #(.width(32)) SP (.D(Input), .en(C_Bus_Enable), .Q(SP_q), .clk(Clock));  // open: clr
  assign Output = B_Enable ? SP_q[23:0] : 24'bz;  // Controlled_Buffer controlled_buffer_1
endmodule

module CPP (
  input  Clock,
  input  [31:0] Input,
  input  B_Enable,
  input  C_Bus_Enable,
  output [23:0] Output
);

  wire [31:0] SP_q;

  Register #(.width(32)) SP (.D(Input), .en(C_Bus_Enable), .Q(SP_q), .clk(Clock));  // open: clr
  assign Output = B_Enable ? SP_q[23:0] : 24'bz;  // Controlled_Buffer controlled_buffer_1
endmodule

module TOS (
  input  Clock,
  input  [31:0] Input,
  input  B_Enable,
  input  C_Bus_Enable,
  output [23:0] Output
);

  wire [31:0] SP_q;

  Register #(.width(32)) SP (.D(Input), .en(C_Bus_Enable), .Q(SP_q), .clk(Clock));  // open: clr
  assign Output = B_Enable ? SP_q[23:0] : 24'bz;  // Controlled_Buffer controlled_buffer_1
endmodule

module OPC (
  input  Clock,
  input  [31:0] Input,
  input  B_Enable,
  input  C_Bus_Enable,
  output [23:0] Output
);

  wire [31:0] SP_q;

  Register #(.width(32)) SP (.D(Input), .en(C_Bus_Enable), .Q(SP_q), .clk(Clock));  // open: clr
  assign Output = B_Enable ? SP_q[23:0] : 24'bz;  // Controlled_Buffer controlled_buffer_1
endmodule

module Shifter (
  input  [31:0] in_1,
  input  [1:0] in_2,
  output [31:0] out_3
);

  wire [31:0] shifter_1_out, shifter_2_out;

  Shifter_part #(.width(32), .shift("ar")) shifter_1 (.in(in_1), .\dist (5'b00001), .out(shifter_1_out));
  Shifter_part #(.width(32)) shifter_2 (.in(in_1), .\dist ({5{1'b0}}), .out(shifter_2_out));
  Multiplexer #(.select(2), .width(32), .enable("false")) multiplexer_1 (
    .in0(in_1), .in1(shifter_1_out), .in2(shifter_2_out), .out(out_3), .sel(in_2));  // open: in3
endmodule

module MAR (
  input  [31:0] in_1,
  input  Enable,
  output [23:0] out_3,
  output [23:0] out_4
);

  wire clock_1_out;
  wire [31:24] register_1_q;

  Clock clock_1 (.out(clock_1_out));
  Register #(.width(32)) register_1 (.D(in_1), .en(Enable), .Q({register_1_q, out_3}), .clk(clock_1_out));  // open: clr

  assign out_4 = out_3;
endmodule

module MBR (
  input  [7:0] Input,
  input  B_Enable_Unsigned,
  input  B_Enable_Signed,
  output [7:0] Output,
  output [31:0] Output_Unsigned,
  output [31:0] Output_Signed,
  output [7:0] Probe
);

  wire Clock_out;
  wire [31:0] bit_extender_1_out, bit_extender_2_out;

  Clock Clock (.out(Clock_out));
  Register MBR (.D(Input), .Q(Output), .clk(Clock_out));  // open: en, clr
  assign bit_extender_1_out = {{24{1'b0}}, Output};  // Bit_Extender bit_extender_1
  assign bit_extender_2_out = {{24{Output[7]}}, Output};  // Bit_Extender bit_extender_2
  assign Output_Unsigned = B_Enable_Unsigned ? bit_extender_1_out : 32'bz;  // Controlled_Buffer controlled_buffer_1
  assign Output_Signed = B_Enable_Signed ? bit_extender_2_out : 32'bz;  // Controlled_Buffer controlled_buffer_2

  assign Probe = Output;
endmodule

module MDR (
  input  [2:0] in_1,
  input  [31:0] in_2,
  input  [31:0] in_3,
  input  in_4,
  input  in_5,
  output [31:0] out_6,
  output [31:0] out_7,
  output [31:0] out_8
);

  wire not_1_out;
  wire [31:0] controlled_buffer_1_out;

  not not_1 (not_1_out, in_4);
  assign controlled_buffer_1_out = not_1_out ? in_2 : 32'bz;  // Controlled_Buffer controlled_buffer_1
  assign controlled_buffer_1_out = in_4 ? in_3 : 32'bz;  // Controlled_Buffer controlled_buffer_2
  Register #(.width(32)) register_1 (.D(controlled_buffer_1_out), .Q(out_8));  // open: en, clk, clr
  assign out_6 = in_5 ? out_8 : 32'bz;  // Controlled_Buffer controlled_buffer_3
  assign out_7 = in_1[2] ? out_8 : 32'bz;  // Controlled_Buffer controlled_buffer_4
endmodule

module PC (
  input  [31:0] in_1,
  input  in_2,
  input  in_3,
  output [23:0] out_4,
  output [31:0] out_5,
  output [31:0] out_6
);

  wire clock_1_out;

  Clock clock_1 (.out(clock_1_out));
  Register #(.width(32)) register_1 (.D(in_1), .en(in_2), .Q({out_6[31:24], out_4}), .clk(clock_1_out));  // open: clr
  assign out_5 = in_3 ? {out_6[31:24], out_4} : 32'bz;  // Controlled_Buffer controlled_buffer_1

  assign out_6[23:0] = out_4;
endmodule

module Control_Store (
  input  [8:0] in_1,
  output [8:0] Addr,
  output [8:0] C_Bus,
  output [2:0] JAM,
  output [7:0] ALU,
  output [2:0] Memory,
  output [3:0] B_Bus
);

  ROM #(.addrWidth(9), .dataWidth(20)) rom_1 (.addr(in_1), .data({Addr, JAM, ALU}));  // open: sel
  ROM #(.addrWidth(9), .dataWidth(16)) rom_2 (.addr(in_1), .data({C_Bus, Memory, B_Bus}));  // open: sel

  // Notes on the sheet:
  //   contents of rom_1 (hex, n*v repeats v):
  //   1000 20835 435 2014 4*0 35 7*0 35 7*0 14
  //   contents of rom_2 (hex, n*v repeats v):
  //   0 211 2140 2140 201 8007 8007 8007 35 7*0 35 7*0 14
  //   512 x 36-Bit Control Store
endmodule
